# Fritzing sketch robot (saved by Fritzing 0.9.3b)
breadboards: 1

parts:
  L1 = Solenoid
  L2 = Solenoid
  L3 = Solenoid
  L4 = Solenoid
  Part1 = Arduino Pro Mini v13
  R1 = Photocell (LDR) [package=THT]
  VCC1 = Battery block 9V
  Motor_A = DC Motor
  Motor_B = DC Motor
  R4 = Photocell (LDR) [package=THT]
  LED2 = LED - 5mm [color="Infrared (940nm)" package="5 mm [THT]"]
  R6 = Resistor [tolerance=±5% resistance=10k package=THT]
  LED1 = LED - 3mm [color="Infrared (940nm)" package="3 mm [THT]"]
  R7 = Resistor [tolerance=±5% resistance=56 package=THT]
  Part3 = Motor Driver 1A Dual TB6612FNG
  R8 = Resistor [tolerance=±5% resistance=10k package=THT]
  R9 = Resistor [tolerance=±5% resistance=330 package=THT]
  Q1 = npn-Powertransistor [package="TO220 [THT]"]
  D1 = Rectifier Diode [part_number=1N4001 package="300 mil [THT]"]

nets:
  N1: L1.pin1, L2.pin1, L3.pin1, L4.pin1, Part1.RAW, VCC1.+, Part3.VM, D1.cathode
  N2: L1.pin2, L2.pin2, L3.pin2, L4.pin2, Q1.collector, D1.anode
  VCC: Part1.VCC, R6.Pin_1, LED1.anode, Part3.VCC, R8.Pin_1
  GND: Part1.GND, R1.pin_1, VCC1.-, R4.pin_1, R7.Pin_0, Part3.GND, Q1.emitter
  N3: Part1.D11_PWM/MOSI, Part3.AIN1
  N4: Part1.D10_PWM/SS, R9.Pin_0
  N5: Part1.D9_PWM, Part3.STBY
  N6: Part1.D8, Part3.BIN2
  N7: Part1.D7, Part3.BIN1
  N8: Part1.D6_PWM, Part3.PWMB
  N9: Part1.D5_PWM, Part3.PWMA
  N10: Part1.D4, Part3.AIN2
  N11: Part1.D3_PWM, R1.pin_0, R8.Pin_0
  N12: Part1.D2, R4.pin_0, R6.Pin_0
  N13: Motor_A.pin_1, Part3.A01
  N14: Motor_A.pin_2, Part3.A02
  N15: Motor_B.pin_1, Part3.B02
  N16: Motor_B.pin_2, Part3.B01
  N17: LED2.cathode, R7.Pin_1
  N18: LED2.anode, LED1.cathode
  N19: R9.Pin_1, Q1.base

custom parts:
  Motor Driver 1A Dual TB6612FNG: The TB6612FNG motor driver can control up to two DC motors at a constant current of 1.2A (3.2A peak). Two input signals (IN1 and IN2) can be used to control the motor in one of four function modes - CW, CCW, short-brake, and stop. The two motor outputs (A and B) can be separately controlled, the speed of each motor is controlled via a PWM input signal with a frequency up to 100kHz. The STBY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

// code stored in the sketch: SOEV.ino
//<define the IO pins for easier Refrencce>
// #define is good for IO pins because #define and IO pins are both hard wiring
#define brkpin 10
#define tachpin 3
//</define the IO pins for easier Refrencce>

//<Init Motor Drivers>
// Creadit where cedit is due - This was copied and pasted from the Sparkfun Hookup Guide
//https://github.com/sparkfun/SparkFun_TB6612FNG_Arduino_Library/blob/master/examples/MotorTestRun/MotorTestRun.ino

// This is the library for the TB6612 that contains the class Motor and all the
// functions
#include <SparkFun_TB6612.h>

// Pins for all inputs, keep in mind the PWM defines must be on PWM pins
// the default pins listed are the ones used on the Redbot (ROB-12097) with
// the exception of STBY which the Redbot controls with a physical switch
#define AIN1 2
#define BIN1 7
#define AIN2 4
#define BIN2 8
#define PWMA 5
#define PWMB 6
#define STBY 9

// these constants are used to allow you to make your motor configuration
// line up with function names like forward.  Value can be 1 or -1
const int offsetA = 1;
const int offsetB = 1;

// Initializing motors.  The library will allow you to initialize as many
// motors as you have memory for.  If you are using functions like forward
// that take 2 motors as arguements you can either write new functions or
// call the function more than once.
Motor prop = Motor(AIN1, AIN2, PWMA, offsetA, STBY);
Motor turn = Motor(BIN1, BIN2, PWMB, offsetB, STBY);
//</Init Motor Drivers>

//<Init Variables>
//Floats are evil due to slow computation speeds. AVOID!
unsigned long trk; //use cm
unsigned long loc; //use cm
const unsigned long decel; //use cm*(cm/ms)
unsigned long spd; //speed in cm/ms
//<used by tachometer>
//global becuase they are used in tachLog() and tachCount()
unsigned long lastTach;
unsigned long thisTach;
//<used by tachCount Function>
//</Init Variables>

void setup() {
  //<turn on LED 13 to signify init>
  pinMode(13, OUTPUT);
  digitalWrite(13, HIGH);
  //</turn on LED 13 to signify init>
  //<pin Modes>
  pinMode(brkpin, OUTPUT);
  pinMode(tachpin, INPUT);
  //</pin Modes>
  attachInterrupt(0, tachLog, RISING); //if the tachpin is pulled high (the light shines through the holes in the wheels)
  //Interrupt is used becuase the code may miss it if it is only called during loop
  prop.drive(255); //turn the motor on
  Serial.println("trk,loc,spd,lastTach,thisTach"); //tells the order of the variables when printed
}

void loop() {
  //<log all the variables for debuging>
  Serial.print(trk);
  Serial.print(",");
  Serial.print(loc);
  Serial.print(",");
  Serial.print(spd);
  Serial.print(",");
  Serial.print(lastTach);
  Serial.print(",");
  Serial.println(thisTach);
  //</log all the variable for debugging>
  tachCount();// do the tach maths
  if (trk - loc <= decel * spd) { //if we are running out of track
    prop.brake(); //brake the motors
    digitalWrite(brkpin, HIGH); //fire the solenoids
  }
}

void tachLog() {//interrupt for tachometer
  lastTach = thisTach;//move thisTach into lastTach to make room for the new reading
  thisTach = millis();// get the new reading
}

void tachCount() {
  //<local variables>
  //I use local variables so that if tachcount is called in the middle of the function it wont make the maths go poof.
  unsigned long lclLast = lastTach;
  unsigned long lclThis = thisTach;
  //</local Variables>
  spd = 1822 / (lclThis - lclLast) * 100; //cm/ms, //1.82212373908208 = dist, //* 100 is to avoid floating point stuff
  if (!(lclThis == thisTach) {//if tachLog has been called since we started
  tachCount();//do this function again
    //I love recursion
  }
}
